# Fritzing sketch Laser_Projection_Microscope (saved by Fritzing 0.9.3b)

parts:
  Nano1 = Arduino Nano v2.3
  J1 = Basic Servo
  J2 = Basic Servo
  LD1 = LD
  J3 = female pin header, 4 pins [form="♀ (female)"]

nets:
  N1: Nano1.D1TX, J3.pin2
  N2: Nano1.D0RX, J3.pin3
  N3: Nano1.RST, LD1.cathode
  N4: Nano1.D2, LD1.anode
  N5: Nano1.D3, J1.pulse
  N6: Nano1.D4, J2.pulse
  VCC: Nano1.+5V, J1.vcc, J2.vcc, J3.pin4
  GND: Nano1.GND, J1.gnd, J2.gnd, J3.pin1

notes:
  Laser servo
  Table servo
  GND \ To Nextion
  RX \ 2.4'' TFT 320x240
  TX / touch screen
  +5V / NX3224T024

custom parts:
  LD: A Generic Red Dot Laser Diode Module (~5mW)
